// Logisim project LC-2200-16.circ as structural Verilog: 2 circuits, main circuit main
module main (
  input  LdPC,
  input  DrPC
);

  wire [15:0] controlled_buffer_1_out, PC_q, undriven;

  Counter #(.width(16), .max('hffff)) PC (.load(LdPC), .D(undriven), .Q(PC_q));  // open: count, carry, clk, clr
  assign controlled_buffer_1_out = DrPC ? PC_q : 16'bz;  // Controlled_Buffer controlled_buffer_1
  RAM #(.addrWidth(16), .dataWidth(16)) ram_1 ();  // open: addr, data, sel, clk, ld, clr
endmodule

module ALUx16 (
  input  [15:0] A,
  input  [15:0] B,
  input  [1:0] func,
  output [15:0] \output 
);

  wire [15:0] adder_1_out, demultiplexer_1_out0, demultiplexer_1_out1, demultiplexer_2_out0,
       demultiplexer_2_out1, nand_1_out;

  Adder #(.width(16)) adder_1 (
    .a(demultiplexer_1_out0), .b(demultiplexer_2_out0), .out(adder_1_out));  // open: cin, cout
  Demultiplexer #(.select(2), .width(16)) demultiplexer_1 (
    .out0(demultiplexer_1_out0), .out1(demultiplexer_1_out1), .in(A), .sel(func));  // open: out2, out3, en
  assign nand_1_out = ~(demultiplexer_1_out1 & demultiplexer_2_out1);  // NAND_Gate nand_1, 16 bits wide
  Multiplexer #(.select(2), .width(16)) multiplexer_1 (
    .in0(adder_1_out), .in1(nand_1_out), .out(\output ), .sel(func));  // open: in2, in3, en
  Demultiplexer #(.select(2), .width(16)) demultiplexer_2 (
    .out0(demultiplexer_2_out0), .out1(demultiplexer_2_out1), .in(B), .sel(func));  // open: out2, out3, en
endmodule
